// Logisim project snake.circ as structural Verilog: 1 circuit, main circuit main
module main (
);

  wire _5, _6, _9, or_1_out, RST;
  wire [3:0] undriven;
  wire [15:0] demultiplexer_1_out0, demultiplexer_1_out1, demultiplexer_1_out2, demultiplexer_1_out3,
       demultiplexer_1_out4, demultiplexer_1_out5, demultiplexer_1_out6, demultiplexer_1_out7,
       demultiplexer_1_out8, demultiplexer_1_out9, demultiplexer_1_out10, demultiplexer_1_out11,
       demultiplexer_1_out12, demultiplexer_1_out13, demultiplexer_1_out14, demultiplexer_1_out15,
       Display_line, n16_x_16_1_out_20, n16_x_16_1_out_21, n16_x_16_1_out_22, n16_x_16_1_out_23,
       n16_x_16_1_out_24, n16_x_16_1_out_25, n16_x_16_1_out_26, n16_x_16_1_out_27, n16_x_16_1_out_28,
       n16_x_16_1_out_29, n16_x_16_1_out_30, n16_x_16_1_out_31, n16_x_16_1_out_32, n16_x_16_1_out_33,
       n16_x_16_1_out_34, n16_x_16_1_out_35, n16_x_16_2_out_20, n16_x_16_2_out_21, n16_x_16_2_out_22,
       n16_x_16_2_out_23, n16_x_16_2_out_24, n16_x_16_2_out_25, n16_x_16_2_out_26, n16_x_16_2_out_27,
       n16_x_16_2_out_28, n16_x_16_2_out_29, n16_x_16_2_out_30, n16_x_16_2_out_31, n16_x_16_2_out_32,
       n16_x_16_2_out_33, n16_x_16_2_out_34, n16_x_16_2_out_35;

  Demultiplexer #(.select(4), .width(16)) demultiplexer_1 (
    .out0(demultiplexer_1_out0), .out1(demultiplexer_1_out1), .out2(demultiplexer_1_out2),
    .out3(demultiplexer_1_out3), .out4(demultiplexer_1_out4), .out5(demultiplexer_1_out5),
    .out6(demultiplexer_1_out6), .out7(demultiplexer_1_out7), .out8(demultiplexer_1_out8),
    .out9(demultiplexer_1_out9), .out10(demultiplexer_1_out10), .out11(demultiplexer_1_out11),
    .out12(demultiplexer_1_out12), .out13(demultiplexer_1_out13), .out14(demultiplexer_1_out14),
    .out15(demultiplexer_1_out15), .in(Display_line), .sel(undriven));  // open: en
  or or_1 (or_1_out, _9, RST);
  _16_x_16 u_16_x_16_1 (
    .in_1(demultiplexer_1_out0), .in_2(demultiplexer_1_out1), .in_3(demultiplexer_1_out2),
    .in_4(demultiplexer_1_out3), .in_5(demultiplexer_1_out4), .in_6(demultiplexer_1_out5),
    .in_7(demultiplexer_1_out6), .in_8(demultiplexer_1_out7), .in_9(demultiplexer_1_out8),
    .in_10(demultiplexer_1_out9), .in_11(demultiplexer_1_out10), .in_12(demultiplexer_1_out11),
    .in_13(demultiplexer_1_out12), .in_14(demultiplexer_1_out13), .in_15(demultiplexer_1_out14),
    .in_16(demultiplexer_1_out15), .clk(_5), .rst(or_1_out), .in_19(undriven), .out_20(n16_x_16_1_out_20),
    .out_21(n16_x_16_1_out_21), .out_22(n16_x_16_1_out_22), .out_23(n16_x_16_1_out_23),
    .out_24(n16_x_16_1_out_24), .out_25(n16_x_16_1_out_25), .out_26(n16_x_16_1_out_26),
    .out_27(n16_x_16_1_out_27), .out_28(n16_x_16_1_out_28), .out_29(n16_x_16_1_out_29),
    .out_30(n16_x_16_1_out_30), .out_31(n16_x_16_1_out_31), .out_32(n16_x_16_1_out_32),
    .out_33(n16_x_16_1_out_33), .out_34(n16_x_16_1_out_34), .out_35(n16_x_16_1_out_35));
  _16_x_16 u_16_x_16_2 (
    .in_1(n16_x_16_1_out_20), .in_2(n16_x_16_1_out_21), .in_3(n16_x_16_1_out_22), .in_4(n16_x_16_1_out_23),
    .in_5(n16_x_16_1_out_24), .in_6(n16_x_16_1_out_25), .in_7(n16_x_16_1_out_26), .in_8(n16_x_16_1_out_27),
    .in_9(n16_x_16_1_out_28), .in_10(n16_x_16_1_out_29), .in_11(n16_x_16_1_out_30),
    .in_12(n16_x_16_1_out_31), .in_13(n16_x_16_1_out_32), .in_14(n16_x_16_1_out_33),
    .in_15(n16_x_16_1_out_34), .in_16(n16_x_16_1_out_35), .clk(_6), .rst(RST), .out_20(n16_x_16_2_out_20),
    .out_21(n16_x_16_2_out_21), .out_22(n16_x_16_2_out_22), .out_23(n16_x_16_2_out_23),
    .out_24(n16_x_16_2_out_24), .out_25(n16_x_16_2_out_25), .out_26(n16_x_16_2_out_26),
    .out_27(n16_x_16_2_out_27), .out_28(n16_x_16_2_out_28), .out_29(n16_x_16_2_out_29),
    .out_30(n16_x_16_2_out_30), .out_31(n16_x_16_2_out_31), .out_32(n16_x_16_2_out_32),
    .out_33(n16_x_16_2_out_33), .out_34(n16_x_16_2_out_34), .out_35(n16_x_16_2_out_35));  // open: in_19
  DotMatrix #(.inputtype("row"), .matrixcols(16), .matrixrows(16)) dotmatrix_1 (
    .row0(n16_x_16_2_out_20), .row1(n16_x_16_2_out_21), .row2(n16_x_16_2_out_22), .row3(n16_x_16_2_out_23),
    .row4(n16_x_16_2_out_24), .row5(n16_x_16_2_out_25), .row6(n16_x_16_2_out_26), .row7(n16_x_16_2_out_27),
    .row8(n16_x_16_2_out_28), .row9(n16_x_16_2_out_29), .row10(n16_x_16_2_out_30), .row11(n16_x_16_2_out_31),
    .row12(n16_x_16_2_out_32), .row13(n16_x_16_2_out_33), .row14(n16_x_16_2_out_34), .row15(n16_x_16_2_out_35));
endmodule
